# Fritzing sketch coruja_gps (saved by Fritzing 1.0.7)

parts:
  Raspberry_Pi_Pico_2_W = Raspberry Pi Pico
  GPS = Generic female header - metal rounded - 4 pins [package=THT]
  Micro_SD = Generic female header - 9 pins [package=THT]
  Display = Generic female header - 8 pins [package=THT]
  Encoder = Generic female header - metal rounded - 5 pins [package=THT]
  Entrada_12V_(pos-chave) = Generic female header - metal rounded - 3 pins [package=THT]
  F1_2A = FUSE [package=fuse_5mm]
  TVS1_P6KE24CA_bidirecional = TVS [package=sma-diode]
  Conversor_step-down_12V->5V_(LM2596_nao_isolado) = Generic female header - metal rounded - 4 pins [package=THT]
  Conector_do_buzzer_(painel)_-_12_V = Generic female header - metal rounded - 2 pins [package=THT]
  LED_RGB_10mm_anodo_comum = RGB LED (com. cathode, rgb) [color="Red (633nm)" current=0.030A package="5 mm [THT]"]
  R1_Vermelho = Resistor [resistance=330 tolerance=±5% power=0.25W package=THT]
  R2_Verde = Resistor [resistance=470 tolerance=±5% power=0.25W package=THT]
  R3_Azul = Resistor [resistance=150 tolerance=±5% power=0.25W package=THT]
  R4_Base_Q1 = Resistor [resistance=1k tolerance=±5% power=0.25W package=THT]
  R5_GPS_RX = Resistor [resistance=1k tolerance=±5% power=0.25W package=THT]
  Q1_BC337 = TRANSISTOR_NPN [package=to-92]
  D1_1N5819 = Schottky Diode [part_number=1N5817 package="300 mil [THT]"]
  D2_1N4148 = Diode [package=diode-1n4148]
  C1_470uF_25V_105C = Electrolytic Capacitor [capacitance=470µF voltage=35V package="200 mil [THT, electrolytic]"]
  C5_470uF_50V_105C = Electrolytic Capacitor [capacitance=470µF voltage=35V package="200 mil [THT, electrolytic]"]
  C2_100nF_(filtro_VSYS) = Ceramic Capacitor [capacitance=100nF voltage=35V package="100 mil [THT, multilayer]"]
  BZ1_SFM-27_(remoto) = Piezo Speaker

nets:
  N1: Raspberry_Pi_Pico_2_W.pin_1, R5_GPS_RX.Pin_0
  N2: Raspberry_Pi_Pico_2_W.pin_2, GPS.pin3
  N3: Raspberry_Pi_Pico_2_W.pin_3, Raspberry_Pi_Pico_2_W.pin_33, Raspberry_Pi_Pico_2_W.pin_38, Raspberry_Pi_Pico_2_W.pin_42, GPS.pin4, Micro_SD.pin2, Display.pin1, Encoder.pin1, Entrada_12V_(pos-chave).pin3, TVS1_P6KE24CA_bidirecional.2, Conversor_step-down_12V->5V_(LM2596_nao_isolado).pin2, Conversor_step-down_12V->5V_(LM2596_nao_isolado).pin4, Q1_BC337.E, C1_470uF_25V_105C.-, C5_470uF_50V_105C.-, C2_100nF_(filtro_VSYS).1
  N4: Raspberry_Pi_Pico_2_W.pin_4, Encoder.pin5
  N5: Raspberry_Pi_Pico_2_W.pin_5, Encoder.pin4
  N6: Raspberry_Pi_Pico_2_W.pin_6, Encoder.pin3
  N7: Raspberry_Pi_Pico_2_W.pin_7, R4_Base_Q1.Pin_0
  N8: Raspberry_Pi_Pico_2_W.pin_9, R3_Azul.Pin_0
  N9: Raspberry_Pi_Pico_2_W.pin_10, R2_Verde.Pin_0
  N10: Raspberry_Pi_Pico_2_W.pin_11, R1_Vermelho.Pin_0
  N11: Raspberry_Pi_Pico_2_W.pin_19, Micro_SD.pin9
  N12: Raspberry_Pi_Pico_2_W.pin_20, Display.pin8
  N13: Raspberry_Pi_Pico_2_W.pin_21, Micro_SD.pin4
  N14: Raspberry_Pi_Pico_2_W.pin_22, Micro_SD.pin6
  N15: Raspberry_Pi_Pico_2_W.pin_24, Micro_SD.pin3, Display.pin3
  N16: Raspberry_Pi_Pico_2_W.pin_25, Micro_SD.pin5, Display.pin4
  N17: Raspberry_Pi_Pico_2_W.pin_26, Display.pin7
  N18: Raspberry_Pi_Pico_2_W.pin_27, Display.pin6
  N19: Raspberry_Pi_Pico_2_W.pin_29, Display.pin5
  N20: Raspberry_Pi_Pico_2_W.pin_36, Micro_SD.pin1, Display.pin2, Encoder.pin2, LED_RGB_10mm_anodo_comum.common_cathode
  N21: Raspberry_Pi_Pico_2_W.pin_39, GPS.pin1, D1_1N5819.cathode, C1_470uF_25V_105C.+, C2_100nF_(filtro_VSYS).0
  N22: GPS.pin2, R5_GPS_RX.Pin_1
  N23: Entrada_12V_(pos-chave).pin1, F1_2A.1
  N24: F1_2A.2, TVS1_P6KE24CA_bidirecional.1, Conversor_step-down_12V->5V_(LM2596_nao_isolado).pin1, Conector_do_buzzer_(painel)_-_12_V.pin1, D2_1N4148.C, C5_470uF_50V_105C.+, BZ1_SFM-27_(remoto).pin1
  N25: Conversor_step-down_12V->5V_(LM2596_nao_isolado).pin3, D1_1N5819.anode
  N26: Conector_do_buzzer_(painel)_-_12_V.pin2, Q1_BC337.C, D2_1N4148.A, BZ1_SFM-27_(remoto).pin2
  N27: LED_RGB_10mm_anodo_comum.red_anode, R1_Vermelho.Pin_1
  N28: LED_RGB_10mm_anodo_comum.green_anode, R2_Verde.Pin_1
  N29: LED_RGB_10mm_anodo_comum.blue_anode, R3_Azul.Pin_1
  N30: R4_Base_Q1.Pin_1, Q1_BC337.B

custom parts:
  Raspberry Pi Pico: Raspberry Pi Pico. Based around the RP2040 microcontroller the Pico is a low cost microcontroller device bringing Raspberry Pi quality, cost, and easy of use to the microcontroller space. Jan 2021, Split part in to two versions: tht (this one) and SMD. This one will drill holes for a .1 in header in pcb to allow plugging in the module as well as providing pads to solder the module to the top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
